# Fritzing sketch esp32_ds18b20 (saved by Fritzing 0.9.3b)

parts:
  U1 = ESP32-38PinWide [part_number=ESP32-38PinWide]
  DS1 = DS18B20 1-Wire Temperature Sensor Probe Cable

nets:
  N1: U1.3.3, DS1.VDD
  N2: U1.GPIO15, DS1.DQ
  GND: U1.GND, DS1.GND

custom parts:
  ESP32-38PinWide: Generic 38-Pin ESP32 with wide format (only access to one side of pins on a breadboard) based on Stephen Lilley's HiLetgo ESP-WROOM-32 ESP32 ESP-32S Development Board.
